// Logisim project main-circuit.circ as structural Verilog
module D_Latch (
  input  D,
  input  Enable,
  output Q,
  output Q_prime
);

  wire nand_1_out, nand_2_out, not_1_out;

  nand nand_1 (nand_1_out, D, Enable);
  nand nand_2 (nand_2_out, Enable, not_1_out);
  not not_1 (not_1_out, D);
  nand nand_3 (Q, nand_1_out, Q_prime);
  nand nand_4 (Q_prime, Q, nand_2_out);
endmodule

module D_FF (
  input  D,
  input  Clk,
  output Q
);

  wire d_latch_1_q, not_1_out;

  D_Latch d_latch_1 (.D(D), .Enable(Clk), .Q(d_latch_1_q));  // open: Q_prime
  D_Latch d_latch_2 (.D(d_latch_1_q), .Enable(not_1_out), .Q(Q));  // open: Q_prime
  not not_1 (not_1_out, Clk);
endmodule
